# Fritzing sketch CanSat_nano (saved by Fritzing 0.9.3b)
breadboards: 2

parts:
  Temp_+_Pressure = Adafruit_BMP280
  Gyro = InvenSense MPU6050  # not connected
  Outside_Temp = LM35 Temperature Sensor [package="TO92 [THT]"]
  XBee = XBee Explorer Regulated
  VCC1 = Battery block 9V
  Part5 = Arduino Nano (Rev3.0)

nets:
  5V: Temp_+_Pressure.VIN, Outside_Temp.+Vs, XBee.5V, Part5.5V
  GND: Temp_+_Pressure.GND, Outside_Temp.GND, XBee.GND, VCC1.-, Part5.GND
  N1: Temp_+_Pressure.SCK/SCL, Part5.D13/SCK
  N2: Temp_+_Pressure.SDO/ADR, Part5.D12/MISO
  N3: Temp_+_Pressure.SDI/SDA, Part5.D11/MOSI
  N4: Temp_+_Pressure.CS, Part5.D10
  N5: Outside_Temp.Vout, Part5.A0
  N6: XBee.DIN, Part5.D1/TX
  N7: XBee.DOUT, Part5.D0/RX
  N8: VCC1.+, Part5.VIN

custom parts:
  Adafruit_BMP280: Bosch has stepped up their game with their new BMP280 sensor, an environmental sensor with temperature, barometric pressure that is the next generation upgrade to the BMP085/BMP180/BMP183. This sensor is great for all sorts of weather sensing and can even be used in both I2C and SPI! This precision sensor from Bosch is the best low-cost, precision sensing solution for measuring barometric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
